// Logisim project Contador_anel_e_johnson.circ as structural Verilog: 1 circuit, main circuit main
module main (
  input  Iniciar_Estado,
  input  Iniciar_Estado_2,
  input  Carregamento,
  input  Carregamento_2,
  input  Iniciar_Estado_3,
  input  Iniciar_Estado_4,
  input  Carregamento_3,
  input  Carregamento_4
);

  wire clock_1_out, clock_2_out, clock_3_out, clock_4_out, controlled_buffer_1_out, controlled_buffer_2_out,
       controlled_buffer_3_out, controlled_buffer_4_out, j_k_ff_1_q, j_k_ff_1_qn, j_k_ff_2_q, j_k_ff_2_qn,
       j_k_ff_3_q, j_k_ff_3_qn, j_k_ff_4_q, j_k_ff_4_qn, j_k_ff_5_q, j_k_ff_5_qn, j_k_ff_6_q, j_k_ff_6_qn,
       j_k_ff_7_q, j_k_ff_7_qn, j_k_ff_8_q, j_k_ff_8_qn, j_k_ff_9_q, j_k_ff_9_qn, j_k_ff_10_q, j_k_ff_10_qn,
       j_k_ff_11_q, j_k_ff_11_qn, j_k_ff_12_q, j_k_ff_12_qn;

  Clock clock_1 (.out(clock_1_out));
  Clock clock_2 (.out(clock_2_out));
  assign controlled_buffer_1_out = Carregamento ? Iniciar_Estado : 1'bz;  // Controlled_Buffer controlled_buffer_1
  assign controlled_buffer_2_out = Carregamento_4 ? Iniciar_Estado_4 : 1'bz;  // Controlled_Buffer controlled_buffer_2
  LED B0 (.in(j_k_ff_1_q));
  J_K_Flip_Flop j_k_ff_1 (
    .J(j_k_ff_5_q), .clk(clock_1_out), .K(j_k_ff_5_qn), .Q(j_k_ff_1_q), .Qn(j_k_ff_1_qn),
    .preset(controlled_buffer_1_out));  // open: en, reset
  LED B0_2 (.in(j_k_ff_2_q));
  J_K_Flip_Flop j_k_ff_2 (
    .J(j_k_ff_6_qn), .clk(clock_2_out), .K(j_k_ff_6_q), .Q(j_k_ff_2_q), .Qn(j_k_ff_2_qn),
    .preset(controlled_buffer_2_out));  // open: en, reset
  LED B1 (.in(j_k_ff_3_q));
  J_K_Flip_Flop j_k_ff_3 (
    .J(j_k_ff_1_q), .clk(clock_1_out), .K(j_k_ff_1_qn), .Q(j_k_ff_3_q), .Qn(j_k_ff_3_qn),
    .reset(controlled_buffer_1_out));  // open: preset, en
  LED B1_2 (.in(j_k_ff_4_q));
  J_K_Flip_Flop j_k_ff_4 (
    .J(j_k_ff_2_q), .clk(clock_2_out), .K(j_k_ff_2_qn), .Q(j_k_ff_4_q), .Qn(j_k_ff_4_qn),
    .reset(controlled_buffer_2_out));  // open: preset, en
  LED B2 (.in(j_k_ff_5_q));
  J_K_Flip_Flop j_k_ff_5 (
    .J(j_k_ff_3_q), .clk(clock_1_out), .K(j_k_ff_3_qn), .Q(j_k_ff_5_q), .Qn(j_k_ff_5_qn),
    .reset(controlled_buffer_1_out));  // open: preset, en
  LED B2_2 (.in(j_k_ff_6_q));
  J_K_Flip_Flop j_k_ff_6 (
    .J(j_k_ff_4_q), .clk(clock_2_out), .K(j_k_ff_4_qn), .Q(j_k_ff_6_q), .Qn(j_k_ff_6_qn),
    .reset(controlled_buffer_2_out));  // open: preset, en
  Clock clock_3 (.out(clock_3_out));
  Clock clock_4 (.out(clock_4_out));
  assign controlled_buffer_3_out = Carregamento_2 ? Iniciar_Estado_2 : 1'bz;  // Controlled_Buffer controlled_buffer_3
  assign controlled_buffer_4_out = Carregamento_3 ? Iniciar_Estado_3 : 1'bz;  // Controlled_Buffer controlled_buffer_4
  LED B2_3 (.in(j_k_ff_7_q));
  J_K_Flip_Flop j_k_ff_7 (
    .J(j_k_ff_9_q), .clk(clock_3_out), .K(j_k_ff_9_qn), .Q(j_k_ff_7_q), .Qn(j_k_ff_7_qn),
    .reset(controlled_buffer_3_out));  // open: preset, en
  LED B2_4 (.in(j_k_ff_8_q));
  J_K_Flip_Flop j_k_ff_8 (
    .J(j_k_ff_10_q), .clk(clock_4_out), .K(j_k_ff_10_qn), .Q(j_k_ff_8_q), .Qn(j_k_ff_8_qn),
    .reset(controlled_buffer_4_out));  // open: preset, en
  J_K_Flip_Flop j_k_ff_9 (
    .J(j_k_ff_11_q), .clk(clock_3_out), .K(j_k_ff_11_qn), .Q(j_k_ff_9_q), .Qn(j_k_ff_9_qn),
    .reset(controlled_buffer_3_out));  // open: preset, en
  LED B1_3 (.in(j_k_ff_10_q));
  J_K_Flip_Flop j_k_ff_10 (
    .J(j_k_ff_12_q), .clk(clock_4_out), .K(j_k_ff_12_qn), .Q(j_k_ff_10_q), .Qn(j_k_ff_10_qn),
    .reset(controlled_buffer_4_out));  // open: preset, en
  LED B1_4 (.in(j_k_ff_9_q));
  LED B0_3 (.in(j_k_ff_11_q));
  J_K_Flip_Flop j_k_ff_11 (
    .J(j_k_ff_7_q), .clk(clock_3_out), .K(j_k_ff_7_qn), .Q(j_k_ff_11_q), .Qn(j_k_ff_11_qn),
    .preset(controlled_buffer_3_out));  // open: en, reset
  LED B0_4 (.in(j_k_ff_12_q));
  J_K_Flip_Flop j_k_ff_12 (
    .J(j_k_ff_8_qn), .clk(clock_4_out), .K(j_k_ff_8_q), .Q(j_k_ff_12_q), .Qn(j_k_ff_12_qn),
    .preset(controlled_buffer_4_out));  // open: en, reset

  // Notes on the sheet:
  //   Ao lado temos a configuração habitual equivalente. 
  //   Ao lado temos a configuração habitual equivalente. 
  //   Contador em anel
  //   Observe que para simplificar o diagrama o bit menos significativo se encontra à esquerda (B0). 
  //   Contador Johnson
  //   Observe que para simplificar o diagrama o bit menos significativo se encontra à esquerda (B0).
  //   Contador em anel
endmodule
