// Logisim project DiagTemp.circ as structural Verilog: 1 circuit, main circuit main
module main (
  input  in_1
);

  wire clock_1_out, clock_2_out, digital_oscilloscope_1_p2, digital_oscilloscope_1_p3,
       digital_oscilloscope_2_p2, digital_oscilloscope_2_p3;

  Clock clock_1 (.out(clock_1_out));
  // Digital_Oscilloscope #(.frontlines("falling")) digital_oscilloscope_1: pin names not known; wires that end beside it: clock_1_out, digital_oscilloscope_1_p2, digital_oscilloscope_1_p3, in_1
  D_Flip_Flop #(.trigger("falling")) d_ff_1 (
    .D(digital_oscilloscope_1_p3), .clk(clock_1_out), .Q(digital_oscilloscope_1_p2),
    .Qn(digital_oscilloscope_1_p3));  // open: preset, reset
  Clock clock_2 (.out(clock_2_out));
  // Digital_Oscilloscope digital_oscilloscope_2: pin names not known; wires that end beside it: clock_2_out, digital_oscilloscope_2_p2, digital_oscilloscope_2_p3, in_1
  D_Flip_Flop d_ff_2 (
    .D(digital_oscilloscope_2_p3), .clk(clock_2_out), .Q(digital_oscilloscope_2_p2),
    .Qn(digital_oscilloscope_2_p3));  // open: preset, reset

  // Notes on the sheet:
  //   Sensível borda de descida
  //   Sensível borda de subida
endmodule
