// Logisim project Elevador.circ as structural Verilog: 1 circuit, main circuit main
module main (
  input  M,
  input  P1,
  input  P2,
  input  P3,
  input  P4,
  output out_6
);

  wire and_1_out, and_2_out, and_3_out, and_4_out, and_5_out, not_1_out, not_2_out, not_3_out, not_4_out,
       not_5_out;

  not not_1 (not_1_out, M);
  not not_2 (not_2_out, P2);
  not not_3 (not_3_out, P1);
  not not_4 (not_4_out, P3);
  not not_5 (not_5_out, P4);
  and and_1 (and_1_out, not_1_out, P1, not_4_out, not_2_out, not_5_out);
  and and_2 (and_2_out, not_1_out, not_3_out, P2, not_4_out, not_5_out);
  and and_3 (and_3_out, not_1_out, not_3_out, not_2_out, P3, not_5_out);
  and and_4 (and_4_out, not_1_out, not_3_out, not_2_out, not_4_out, P4);
  and and_5 (and_5_out, M, not_3_out, not_2_out, not_4_out, not_5_out);
  or or_1 (out_6, and_1_out, and_2_out, and_3_out, and_4_out, and_5_out);
endmodule
