// Logisim project Estrutura4x2.circ as structural Verilog: 1 circuit, main circuit main
module main (
  input  in_1,
  input  in_2,
  input  CS,
  input  R_nW,
  input  OE,
  input  in_6,
  input  in_7,
  input  CLEAR,
  output OUTPUT,
  output out_10
);

  wire and_1_out, and_2_out, and_3_out, and_4_out, and_5_out, and_6_out, and_7_out, and_8_out, and_9_out,
       and_10_out, and_11_out, and_12_out, and_13_out, and_14_out, and_15_out, and_16_out, and_17_out,
       and_18_out, d_ff_1_q, d_ff_2_q, d_ff_3_q, d_ff_4_q, d_ff_5_q, d_ff_6_q, d_ff_7_q, d_ff_8_q, or_1_out,
       or_2_out;

  and and_1 (and_1_out, ~in_7, ~in_6);  // AND_Gate
  and and_2 (and_2_out, in_7, ~in_6);  // AND_Gate
  and and_3 (and_3_out, ~in_7, in_6);  // AND_Gate
  and and_4 (and_4_out, in_7, in_6);
  and and_5 (and_5_out, and_9_out, and_1_out);
  and and_6 (and_6_out, and_9_out, and_2_out);
  and and_7 (and_7_out, and_9_out, and_3_out);
  and and_8 (and_8_out, and_9_out, and_4_out);
  and and_9 (and_9_out, CS, ~R_nW);  // AND_Gate
  and and_10 (and_10_out, OE, R_nW, CS);
  D_Flip_Flop d_ff_1 (.clk(and_5_out), .D(in_1), .Q(d_ff_1_q), .reset(CLEAR));  // open: Qn, preset, en
  D_Flip_Flop d_ff_2 (.clk(and_6_out), .D(in_1), .Q(d_ff_2_q), .reset(CLEAR));  // open: Qn, preset, en
  D_Flip_Flop d_ff_3 (.clk(and_7_out), .D(in_1), .Q(d_ff_3_q), .reset(CLEAR));  // open: Qn, preset, en
  D_Flip_Flop d_ff_4 (.clk(and_8_out), .D(in_1), .Q(d_ff_4_q), .reset(CLEAR));  // open: Qn, preset, en
  and and_11 (and_11_out, d_ff_1_q, and_1_out);
  and and_12 (and_12_out, d_ff_2_q, and_2_out);
  and and_13 (and_13_out, d_ff_3_q, and_3_out);
  and and_14 (and_14_out, d_ff_4_q, and_4_out);
  or or_1 (or_1_out, and_14_out, and_13_out, and_12_out, and_11_out);
  D_Flip_Flop d_ff_5 (.clk(and_5_out), .D(in_2), .Q(d_ff_5_q), .reset(CLEAR));  // open: Qn, preset, en
  D_Flip_Flop d_ff_6 (.clk(and_6_out), .D(in_2), .Q(d_ff_6_q), .reset(CLEAR));  // open: Qn, preset, en
  D_Flip_Flop d_ff_7 (.clk(and_7_out), .D(in_2), .Q(d_ff_7_q), .reset(CLEAR));  // open: Qn, preset, en
  D_Flip_Flop d_ff_8 (.clk(and_8_out), .D(in_2), .Q(d_ff_8_q), .reset(CLEAR));  // open: Qn, preset, en
  and and_15 (and_15_out, d_ff_5_q, and_1_out);
  and and_16 (and_16_out, d_ff_6_q, and_2_out);
  and and_17 (and_17_out, d_ff_7_q, and_3_out);
  and and_18 (and_18_out, d_ff_8_q, and_4_out);
  or or_2 (or_2_out, and_18_out, and_17_out, and_16_out, and_15_out);
  assign OUTPUT = and_10_out ? or_1_out : 1'bz;  // Controlled_Buffer controlled_buffer_1
  assign out_10 = and_10_out ? or_2_out : 1'bz;  // Controlled_Buffer controlled_buffer_2

  // Notes on the sheet:
  //   POSIÇÃO DE MEMÓRIA
  //   <                                 DADOS                               >
endmodule
