// Logisim project Estrutura4x4LOGISIM_Clock.circ as structural Verilog: 1 circuit, main circuit main
module main (
  input  in_1,
  input  in_2,
  input  in_3,
  input  in_4,
  input  [1:0] in_5,
  input  R_nW,
  input  O_E,
  output [3:0] out_8
);

  wire _0, _1, _2, _3, and_1_out, and_2_out, and_3_out, and_4_out, and_5_out, and_6_out, and_7_out,
       and_8_out, and_9_out, and_10_out, and_11_out, and_12_out, and_13_out, and_14_out, and_15_out,
       and_16_out, and_17_out, clock_1_out, d_ff_1_q, d_ff_2_q, d_ff_3_q, d_ff_4_q, d_ff_5_q, d_ff_6_q,
       d_ff_7_q, d_ff_8_q, d_ff_9_q, d_ff_10_q, d_ff_11_q, d_ff_12_q, d_ff_13_q, d_ff_14_q, d_ff_15_q,
       d_ff_16_q, multiplexer_1_out, or_1_out, or_2_out, or_3_out, or_4_out;
  wire [3:0] controlled_buffer_1_out;

  Demultiplexer #(.select(2)) demultiplexer_1 (
    .out0(_0), .out1(_1), .out2(_2), .out3(_3), .in(multiplexer_1_out), .sel(in_5));  // open: en
  Multiplexer #(.select(2)) multiplexer_1 (
    .in0(1'b1), .in1(1'b1), .in2(1'b1), .in3(1'b1), .out(multiplexer_1_out), .sel(in_5));  // open: en
  and and_1 (and_1_out, O_E, ~R_nW);  // AND_Gate
  Clock clock_1 (.out(clock_1_out));
  assign controlled_buffer_1_out = R_nW ? {_3, _2, _1, _0} : 4'bz;  // Controlled_Buffer controlled_buffer_1
  Pull_Resistor pull_resistor_1 (.node(controlled_buffer_1_out));
  D_Flip_Flop d_ff_1 (
    .clk(clock_1_out), .D(in_1), .Q(d_ff_1_q), .en(controlled_buffer_1_out[0]));  // open: Qn, preset, reset
  D_Flip_Flop d_ff_2 (
    .clk(clock_1_out), .D(in_1), .Q(d_ff_2_q), .en(controlled_buffer_1_out[1]));  // open: Qn, preset, reset
  D_Flip_Flop d_ff_3 (
    .clk(clock_1_out), .D(in_1), .Q(d_ff_3_q), .en(controlled_buffer_1_out[2]));  // open: Qn, preset, reset
  D_Flip_Flop d_ff_4 (
    .clk(clock_1_out), .D(in_1), .Q(d_ff_4_q), .en(controlled_buffer_1_out[3]));  // open: Qn, preset, reset
  and and_2 (and_2_out, _3, d_ff_4_q);
  and and_3 (and_3_out, _1, d_ff_2_q);
  and and_4 (and_4_out, _2, d_ff_3_q);
  or or_1 (or_1_out, and_2_out, and_4_out, and_3_out, and_5_out);
  and and_5 (and_5_out, _0, d_ff_1_q);
  assign out_8[3] = and_1_out ? or_1_out : 1'bz;  // Controlled_Buffer controlled_buffer_2
  D_Flip_Flop d_ff_5 (
    .clk(clock_1_out), .D(in_2), .Q(d_ff_5_q), .en(controlled_buffer_1_out[0]));  // open: Qn, preset, reset
  D_Flip_Flop d_ff_6 (
    .clk(clock_1_out), .D(in_2), .Q(d_ff_6_q), .en(controlled_buffer_1_out[1]));  // open: Qn, preset, reset
  D_Flip_Flop d_ff_7 (
    .clk(clock_1_out), .D(in_2), .Q(d_ff_7_q), .en(controlled_buffer_1_out[2]));  // open: Qn, preset, reset
  D_Flip_Flop d_ff_8 (
    .clk(clock_1_out), .D(in_2), .Q(d_ff_8_q), .en(controlled_buffer_1_out[3]));  // open: Qn, preset, reset
  and and_6 (and_6_out, _2, d_ff_7_q);
  and and_7 (and_7_out, _3, d_ff_8_q);
  or or_2 (or_2_out, and_7_out, and_6_out, and_8_out, and_9_out);
  assign out_8[2] = and_1_out ? or_2_out : 1'bz;  // Controlled_Buffer controlled_buffer_3
  and and_8 (and_8_out, _1, d_ff_6_q);
  and and_9 (and_9_out, _0, d_ff_5_q);
  D_Flip_Flop d_ff_9 (
    .clk(clock_1_out), .D(in_3), .Q(d_ff_9_q), .en(controlled_buffer_1_out[0]));  // open: Qn, preset, reset
  D_Flip_Flop d_ff_10 (
    .clk(clock_1_out), .D(in_3), .Q(d_ff_10_q), .en(controlled_buffer_1_out[1]));  // open: Qn, preset, reset
  D_Flip_Flop d_ff_11 (
    .clk(clock_1_out), .D(in_3), .Q(d_ff_11_q), .en(controlled_buffer_1_out[2]));  // open: Qn, preset, reset
  D_Flip_Flop d_ff_12 (
    .clk(clock_1_out), .D(in_3), .Q(d_ff_12_q), .en(controlled_buffer_1_out[3]));  // open: Qn, preset, reset
  and and_10 (and_10_out, _3, d_ff_12_q);
  assign out_8[1] = and_1_out ? or_3_out : 1'bz;  // Controlled_Buffer controlled_buffer_4
  and and_11 (and_11_out, _0, d_ff_9_q);
  and and_12 (and_12_out, _1, d_ff_10_q);
  and and_13 (and_13_out, _2, d_ff_11_q);
  or or_3 (or_3_out, and_10_out, and_13_out, and_12_out, and_11_out);
  D_Flip_Flop d_ff_13 (
    .clk(clock_1_out), .D(in_4), .Q(d_ff_13_q), .en(controlled_buffer_1_out[0]));  // open: Qn, preset, reset
  D_Flip_Flop d_ff_14 (
    .clk(clock_1_out), .D(in_4), .Q(d_ff_14_q), .en(controlled_buffer_1_out[1]));  // open: Qn, preset, reset
  D_Flip_Flop d_ff_15 (
    .clk(clock_1_out), .D(in_4), .Q(d_ff_15_q), .en(controlled_buffer_1_out[2]));  // open: Qn, preset, reset
  D_Flip_Flop d_ff_16 (
    .clk(clock_1_out), .D(in_4), .Q(d_ff_16_q), .en(controlled_buffer_1_out[3]));  // open: Qn, preset, reset
  assign out_8[0] = and_1_out ? or_4_out : 1'bz;  // Controlled_Buffer controlled_buffer_5
  and and_14 (and_14_out, _2, d_ff_15_q);
  and and_15 (and_15_out, _3, d_ff_16_q);
  and and_16 (and_16_out, _1, d_ff_14_q);
  or or_4 (or_4_out, and_15_out, and_14_out, and_16_out, and_17_out);
  and and_17 (and_17_out, _0, d_ff_13_q);
  Hex_Digit_Display hex_digit_display_1 (.value(out_8));  // open: dp
endmodule
