// Logisim project Ex.Tec.circ as structural Verilog: 1 circuit, main circuit main
module main (
);

  wire and_1_out, clock_1_out, clock_2_out, j_k_ff_1_q, j_k_ff_2_q, j_k_ff_3_q, j_k_ff_3_qn, j_k_ff_4_qn,
       j_k_ff_5_q, j_k_ff_6_q, j_k_ff_6_qn, or_1_out, or_2_out, xnor_1_out, xor_1_out;

  Clock clock_1 (.out(clock_1_out));
  Clock clock_2 (.out(clock_2_out));
  J_K_Flip_Flop j_k_ff_1 (
    .J(j_k_ff_4_qn), .K(j_k_ff_4_qn), .clk(clock_1_out), .Q(j_k_ff_1_q));  // open: Qn, preset, reset
  and and_1 (and_1_out, j_k_ff_5_q, j_k_ff_6_qn);
  or or_1 (or_1_out, j_k_ff_1_q, j_k_ff_4_qn);
  J_K_Flip_Flop j_k_ff_2 (.J(1'b1), .K(or_1_out), .clk(clock_1_out), .Q(j_k_ff_2_q));  // open: Qn, preset, reset
  J_K_Flip_Flop j_k_ff_3 (
    .J(and_1_out), .K(j_k_ff_6_qn), .clk(clock_2_out), .Q(j_k_ff_3_q), .Qn(j_k_ff_3_qn));  // open: preset, reset
  J_K_Flip_Flop j_k_ff_4 (.J(1'b1), .K(j_k_ff_2_q), .clk(clock_1_out), .Qn(j_k_ff_4_qn));  // open: Q, preset, reset
  J_K_Flip_Flop j_k_ff_5 (.J(1'b1), .K(xnor_1_out), .clk(clock_2_out), .Q(j_k_ff_5_q));  // open: Qn, preset, reset
  xnor xnor_1 (xnor_1_out, j_k_ff_3_q, j_k_ff_6_q);
  xor xor_1 (xor_1_out, j_k_ff_5_q, j_k_ff_3_q);
  or or_2 (or_2_out, j_k_ff_3_qn, j_k_ff_5_q);
  J_K_Flip_Flop j_k_ff_6 (
    .J(xor_1_out), .K(or_2_out), .clk(clock_2_out), .Q(j_k_ff_6_q), .Qn(j_k_ff_6_qn));  // open: preset, reset
endmodule
