// Logisim project ExampleASCII_MUX.circ as structural Verilog: 7 circuits, main circuit main
module main (
  input  in_1,
  input  in_2,
  input  [4:0] in_3,
  input  [4:0] in_4,
  input  [4:0] in_5,
  input  [4:0] in_6,
  input  [4:0] in_7,
  input  [4:0] in_8,
  input  [4:0] in_9
);

  wire and_1_out, clock_1_out, clock_2_out;
  wire [2:0] j_k_ff_3_q;
  wire [4:0] multiplexer_1_out;
  wire [6:0] bits_1_ascii;

  Multiplexer #(.select(3), .width(5)) multiplexer_1 (
    .in0(in_3), .in1(in_4), .in2(in_5), .in3(in_6), .in4(in_7), .in5(in_8), .in6(in_9), .in7(in_4),
    .out(multiplexer_1_out), .sel(j_k_ff_3_q));
  Clock clock_1 (.out(clock_1_out));
  J_K_Flip_Flop j_k_ff_1 (
    .J(and_1_out), .K(and_1_out), .clk(clock_1_out), .Q(j_k_ff_3_q[2]));  // open: Qn, preset, reset
  J_K_Flip_Flop j_k_ff_2 (
    .J(j_k_ff_3_q[0]), .K(j_k_ff_3_q[0]), .clk(clock_1_out), .Q(j_k_ff_3_q[1]));  // open: Qn, preset, reset
  and and_1 (and_1_out, j_k_ff_3_q[0], j_k_ff_3_q[1]);
  J_K_Flip_Flop j_k_ff_3 (.J(1'b1), .K(1'b1), .clk(clock_1_out), .Q(j_k_ff_3_q[0]));  // open: Qn, preset, reset
  Clock clock_2 (.out(clock_2_out));
  TTY tty_1 (.data(bits_1_ascii), .clk(clock_2_out), .we(in_1), .clr(in_2));
  bits bits_1 (.ENTRADA(multiplexer_1_out), .HABILITAR(in_1), .ASCII(bits_1_ascii));
endmodule

module bit_0 (
  input  [4:0] SEL,
  output out_2
);

  Multiplexer #(.select(5)) multiplexer_1 (
    .in0(1'b0), .in1(1'b1), .in2(1'b0), .in3(1'b1), .in4(1'b0), .in5(1'b1), .in6(1'b0), .in7(1'b1),
    .in8(1'b0), .in9(1'b1), .in10(1'b0), .in11(1'b1), .in12(1'b0), .in13(1'b1), .in14(1'b0), .in15(1'b1),
    .in16(1'b0), .in17(1'b1), .in18(1'b0), .in19(1'b1), .in20(1'b0), .in21(1'b1), .in22(1'b0), .in23(1'b1),
    .in24(1'b0), .in25(1'b1), .in26(1'b0), .in27(1'b0), .in28(1'b0), .in29(1'b0), .in30(1'b0), .in31(1'b0),
    .out(out_2), .sel(SEL));
endmodule

module bit_1 (
  input  [4:0] SEL,
  output out_2
);

  Multiplexer #(.select(5)) multiplexer_1 (
    .in0(1'b0), .in1(1'b0), .in2(1'b1), .in3(1'b1), .in4(1'b0), .in5(1'b0), .in6(1'b1), .in7(1'b1),
    .in8(1'b0), .in9(1'b0), .in10(1'b1), .in11(1'b1), .in12(1'b0), .in13(1'b0), .in14(1'b1), .in15(1'b1),
    .in16(1'b0), .in17(1'b0), .in18(1'b1), .in19(1'b1), .in20(1'b0), .in21(1'b0), .in22(1'b1), .in23(1'b1),
    .in24(1'b0), .in25(1'b0), .in26(1'b1), .in27(1'b0), .in28(1'b0), .in29(1'b0), .in30(1'b0), .in31(1'b0),
    .out(out_2), .sel(SEL));
endmodule

module bit_2 (
  input  [4:0] SEL,
  output out_2
);

  Multiplexer #(.select(5)) multiplexer_1 (
    .in0(1'b0), .in1(1'b0), .in2(1'b0), .in3(1'b0), .in4(1'b1), .in5(1'b1), .in6(1'b1), .in7(1'b1),
    .in8(1'b0), .in9(1'b0), .in10(1'b0), .in11(1'b0), .in12(1'b1), .in13(1'b1), .in14(1'b1), .in15(1'b1),
    .in16(1'b0), .in17(1'b0), .in18(1'b0), .in19(1'b0), .in20(1'b1), .in21(1'b1), .in22(1'b1), .in23(1'b1),
    .in24(1'b0), .in25(1'b0), .in26(1'b0), .in27(1'b0), .in28(1'b0), .in29(1'b0), .in30(1'b0), .in31(1'b0),
    .out(out_2), .sel(SEL));
endmodule

module bit_3 (
  input  [4:0] SEL,
  output out_2
);

  Multiplexer #(.select(5)) multiplexer_1 (
    .in0(1'b0), .in1(1'b0), .in2(1'b0), .in3(1'b0), .in4(1'b0), .in5(1'b0), .in6(1'b0), .in7(1'b0),
    .in8(1'b1), .in9(1'b1), .in10(1'b1), .in11(1'b1), .in12(1'b1), .in13(1'b1), .in14(1'b1), .in15(1'b1),
    .in16(1'b0), .in17(1'b0), .in18(1'b0), .in19(1'b0), .in20(1'b0), .in21(1'b0), .in22(1'b0), .in23(1'b0),
    .in24(1'b1), .in25(1'b1), .in26(1'b1), .in27(1'b0), .in28(1'b0), .in29(1'b0), .in30(1'b0), .in31(1'b0),
    .out(out_2), .sel(SEL));
endmodule

module bit_4 (
  input  [4:0] SEL,
  output out_2
);

  Multiplexer #(.select(5)) multiplexer_1 (
    .in0(1'b0), .in1(1'b0), .in2(1'b0), .in3(1'b0), .in4(1'b0), .in5(1'b0), .in6(1'b0), .in7(1'b0),
    .in8(1'b0), .in9(1'b0), .in10(1'b0), .in11(1'b0), .in12(1'b0), .in13(1'b0), .in14(1'b0), .in15(1'b0),
    .in16(1'b1), .in17(1'b1), .in18(1'b1), .in19(1'b1), .in20(1'b1), .in21(1'b1), .in22(1'b1), .in23(1'b1),
    .in24(1'b1), .in25(1'b1), .in26(1'b1), .in27(1'b0), .in28(1'b0), .in29(1'b0), .in30(1'b0), .in31(1'b0),
    .out(out_2), .sel(SEL));
endmodule

module bits (
  input  [4:0] ENTRADA,
  input  HABILITAR,
  output [6:0] ASCII
);

  wire [4:0] bit_0_1_out_2;

  bit_0 bit_0_1 (.SEL(ENTRADA), .out_2(bit_0_1_out_2[0]));
  bit_1 bit_1_1 (.SEL(ENTRADA), .out_2(bit_0_1_out_2[1]));
  bit_2 bit_2_1 (.SEL(ENTRADA), .out_2(bit_0_1_out_2[2]));
  bit_3 bit_3_1 (.SEL(ENTRADA), .out_2(bit_0_1_out_2[3]));
  bit_4 bit_4_1 (.SEL(ENTRADA), .out_2(bit_0_1_out_2[4]));
  Demultiplexer #(.disabled("Z"), .width(7)) demultiplexer_1 (
    .out1(ASCII), .in({2'b10, bit_0_1_out_2}), .sel(HABILITAR));  // open: out0

  // Notes on the sheet:
  //   ENTRADA: pull=down
endmodule
