// Logisim project JK.circ as structural Verilog: 1 circuit, main circuit main
module main (
  input  in_1,
  input  in_2,
  input  in_3,
  input  in_4,
  output out_5,
  output out_6
);

  wire clock_1_out;

  Clock clock_1 (.out(clock_1_out));
  J_K_Flip_Flop j_k_ff_1 (.J(in_2), .K(in_3), .clk(clock_1_out), .Q(out_5), .Qn(out_6), .preset(in_1), .reset(in_4));
endmodule
