// Logisim project LSD_7Seg.circ as structural Verilog: 8 circuits, main circuit circ_A
module circ_A (
  input  A,
  input  B,
  input  C,
  input  D,
  output F
);

  wire and_1_out, and_2_out, and_3_out, and_4_out, not_1_out, not_2_out, not_3_out, not_4_out;

  not not_1 (not_1_out, A);
  not not_2 (not_2_out, B);
  not not_3 (not_3_out, C);
  not not_4 (not_4_out, D);
  and and_1 (and_1_out, not_1_out, C);
  and and_2 (and_2_out, not_1_out, B, D);
  and and_3 (and_3_out, A, not_2_out, not_3_out);
  and and_4 (and_4_out, not_1_out, not_2_out, not_4_out);
  or or_1 (F, and_1_out, and_2_out, and_3_out, and_4_out);
endmodule

module circ_B (
  input  A,
  input  B,
  input  C,
  input  D,
  output F
);

  wire and_1_out, and_2_out, and_3_out, and_4_out, not_1_out, not_2_out, not_3_out, not_4_out;

  not not_1 (not_1_out, A);
  not not_2 (not_2_out, B);
  not not_3 (not_3_out, C);
  not not_4 (not_4_out, D);
  and and_1 (and_1_out, not_1_out, not_2_out);
  and and_2 (and_2_out, not_1_out, not_3_out, not_4_out);
  and and_3 (and_3_out, not_1_out, C, D);
  and and_4 (and_4_out, not_2_out, not_3_out);
  or or_1 (F, and_1_out, and_2_out, and_3_out, and_4_out);
endmodule

module circ_C (
  input  A,
  input  B,
  input  C,
  input  D,
  output F
);

  wire and_1_out, and_2_out, and_3_out, not_1_out, not_2_out, not_3_out;

  not not_1 (not_1_out, A);
  not not_2 (not_2_out, B);
  not not_3 (not_3_out, C);
  and and_1 (and_1_out, not_1_out, D);
  and and_2 (and_2_out, not_1_out, B);
  and and_3 (and_3_out, not_2_out, not_3_out);
  or or_1 (F, and_1_out, and_2_out, and_3_out);
endmodule

module circ_D (
  input  A,
  input  B,
  input  C,
  input  D,
  output F
);

  wire and_1_out, and_2_out, and_3_out, and_4_out, and_5_out, not_1_out, not_2_out, not_3_out, not_4_out;

  not not_1 (not_1_out, A);
  not not_2 (not_2_out, B);
  not not_3 (not_3_out, C);
  not not_4 (not_4_out, D);
  and and_1 (and_1_out, not_1_out, not_2_out, C);
  and and_2 (and_2_out, not_1_out, B, not_3_out, D);
  and and_3 (and_3_out, not_1_out, C, not_4_out);
  and and_4 (and_4_out, A, not_2_out, not_3_out);
  and and_5 (and_5_out, not_1_out, not_2_out, not_4_out);
  or or_1 (F, and_1_out, and_2_out, and_3_out, and_4_out, and_5_out);
endmodule

module circ_E (
  input  A,
  input  B,
  input  C,
  input  D,
  output F
);

  wire and_1_out, and_2_out, not_1_out, not_2_out, not_3_out, not_4_out;

  not not_1 (not_1_out, A);
  not not_2 (not_2_out, B);
  not not_3 (not_3_out, C);
  not not_4 (not_4_out, D);
  and and_1 (and_1_out, not_1_out, C, not_4_out);
  and and_2 (and_2_out, not_2_out, not_3_out, not_4_out);
  or or_1 (F, and_1_out, and_2_out);
endmodule

module circ_F (
  input  A,
  input  B,
  input  C,
  input  D,
  output F
);

  wire and_1_out, and_2_out, and_3_out, and_4_out, not_1_out, not_2_out, not_3_out, not_4_out;

  not not_1 (not_1_out, A);
  not not_2 (not_2_out, B);
  not not_3 (not_3_out, C);
  not not_4 (not_4_out, D);
  and and_1 (and_1_out, not_1_out, B, not_3_out);
  and and_2 (and_2_out, not_1_out, B, not_4_out);
  and and_3 (and_3_out, A, not_2_out, not_3_out);
  and and_4 (and_4_out, not_1_out, not_3_out, not_4_out);
  or or_1 (F, and_1_out, and_2_out, and_3_out, and_4_out);
endmodule

module circ_G (
  input  A,
  input  B,
  input  C,
  input  D,
  output F
);

  wire and_1_out, and_2_out, and_3_out, and_4_out, not_1_out, not_2_out, not_3_out, not_4_out;

  not not_1 (not_1_out, A);
  not not_2 (not_2_out, B);
  not not_3 (not_3_out, C);
  not not_4 (not_4_out, D);
  and and_1 (and_1_out, not_1_out, not_2_out, C);
  and and_2 (and_2_out, not_1_out, B, not_3_out);
  and and_3 (and_3_out, A, not_2_out, not_3_out);
  and and_4 (and_4_out, not_1_out, C, not_4_out);
  or or_1 (F, and_1_out, and_2_out, and_3_out, and_4_out);
endmodule

module cir_Main (
  input  A,
  input  B,
  input  C,
  input  D
);

  wire circ_a_1_f, circ_b_1_f, circ_c_1_f, circ_d_1_f, circ_e_1_f, circ_f_1_f, circ_g_1_f;

  circ_A circ_a_1 (.A(A), .B(B), .C(C), .D(D), .F(circ_a_1_f));
  circ_B circ_b_1 (.A(A), .B(B), .C(C), .D(D), .F(circ_b_1_f));
  circ_C circ_c_1 (.A(A), .B(B), .C(C), .D(D), .F(circ_c_1_f));
  circ_D circ_d_1 (.A(A), .B(B), .C(C), .D(D), .F(circ_d_1_f));
  circ_E circ_e_1 (.A(A), .B(B), .C(C), .D(D), .F(circ_e_1_f));
  circ_F circ_f_1 (.A(A), .B(B), .C(C), .D(D), .F(circ_f_1_f));
  circ_G circ_g_1 (.A(A), .B(B), .C(C), .D(D), .F(circ_g_1_f));
  _7_Segment_Display u_7_segment_display_1 (
    .g(circ_g_1_f), .f(circ_f_1_f), .a(circ_a_1_f), .b(circ_b_1_f), .e(circ_e_1_f), .d(circ_d_1_f),
    .c(circ_c_1_f));  // open: dp
endmodule
