// Logisim project LeituraParSerial.circ as structural Verilog: 1 circuit, main circuit main
module main (
  input  in_1,
  input  in_2,
  input  EDE,
  input  EDD,
  input  in_5,
  input  in_6,
  input  in_7,
  input  [3:0] in_8,
  output out_9,
  output out_10,
  output out_11,
  output out_12,
  output SaidaE,
  output [3:0] out_14,
  output SaidaD
);

  wire clock_1_out, D1, D2, multiplexer_1_out, multiplexer_2_out, multiplexer_3_out, multiplexer_4_out;

  Clock clock_1 (.out(clock_1_out));
  // Shift_Register #(.length(4), .parallel("false")) LEITURAE: pin names not known; wires that end beside it: in_1, clock_1_out, SaidaE
  Multiplexer #(.select(2)) multiplexer_1 (
    .in0(SaidaE), .in1(EDD), .in2(D2), .in3(in_8[3]), .out(multiplexer_1_out), .sel({in_6, in_7}));
  LED led_1 (.in(SaidaE));
  D_Flip_Flop d_ff_1 (.D(multiplexer_1_out), .clk(clock_1_out), .Q(SaidaE));  // open: Qn, preset, reset
  assign out_9 = in_2 ? SaidaE : 1'bz;  // Controlled_Buffer controlled_buffer_1
  D_Flip_Flop d_ff_2 (.D(multiplexer_2_out), .clk(clock_1_out), .Q(D2));  // open: Qn, preset, reset
  Multiplexer #(.select(2)) multiplexer_2 (
    .in0(D2), .in1(SaidaE), .in2(D1), .in3(in_8[2]), .out(multiplexer_2_out), .sel({in_6, in_7}));
  assign out_10 = in_2 ? D2 : 1'bz;  // Controlled_Buffer controlled_buffer_2
  LED led_2 (.in(D2));
  Multiplexer #(.select(2)) multiplexer_3 (
    .in0(D1), .in1(D2), .in2(SaidaD), .in3(in_8[1]), .out(multiplexer_3_out), .sel({in_6, in_7}));
  LED led_3 (.in(D1));
  D_Flip_Flop d_ff_3 (.D(multiplexer_3_out), .clk(clock_1_out), .Q(D1));  // open: Qn, preset, reset
  assign out_11 = in_2 ? D1 : 1'bz;  // Controlled_Buffer controlled_buffer_3
  D_Flip_Flop d_ff_4 (.D(multiplexer_4_out), .clk(clock_1_out), .Q(SaidaD));  // open: Qn, preset, reset
  Multiplexer #(.select(2)) multiplexer_4 (
    .in0(SaidaD), .in1(D1), .in2(EDE), .in3(in_8[0]), .out(multiplexer_4_out), .sel({in_6, in_7}));
  assign out_12 = in_2 ? SaidaD : 1'bz;  // Controlled_Buffer controlled_buffer_4
  LED led_4 (.in(SaidaD));
  // Shift_Register #(.length(4), .parallel("false")) LEITURAD: pin names not known; wires that end beside it: in_5, clock_1_out, SaidaD
  Register #(.width(4)) register_1 (.D({SaidaE, D2, D1, SaidaD}), .en(1'b1), .clk(in_2), .Q(out_14));  // open: clr

  // Other names for the same wires on the sheet: D0 = SaidaD; D3 = SaidaE; LER = in_2

  // Notes on the sheet:
  //   MANTEM O ESTADO - CONTROLE 0
  //   EDD - CONTROLE 1
  //   EDE - CONTROLE 2
  //   ARMAZENAR - CONTROLE 3
endmodule
