// Logisim project LeituraParSerial2.circ as structural Verilog: 1 circuit, main circuit main
module main (
  input  E,
  input  D,
  input  [1:0] in_3,
  input  [3:0] in_4
);

  wire button_1_out, clock_1_out, d_ff_1_q, d_ff_2_q, d_ff_3_q, d_ff_4_q, multiplexer_1_out,
       multiplexer_2_out, multiplexer_3_out, multiplexer_4_out;
  wire [3:0] controlled_buffer_4_out;

  Button button_1 (.out(button_1_out));
  Clock clock_1 (.out(clock_1_out));
  Multiplexer #(.select(2)) multiplexer_1 (
    .in0(d_ff_1_q), .in1(D), .in2(d_ff_2_q), .in3(in_4[3]), .out(multiplexer_1_out), .sel(in_3));
  LED SaiEsq (.in(d_ff_1_q));
  D_Flip_Flop d_ff_1 (.D(multiplexer_1_out), .clk(clock_1_out), .Q(d_ff_1_q));  // open: Qn, preset, reset
  assign controlled_buffer_4_out[3] = button_1_out ? d_ff_1_q : 1'bz;  // Controlled_Buffer controlled_buffer_1
  Multiplexer #(.select(2)) multiplexer_2 (
    .in0(d_ff_2_q), .in1(d_ff_1_q), .in2(d_ff_3_q), .in3(in_4[2]), .out(multiplexer_2_out), .sel(in_3));
  D_Flip_Flop d_ff_2 (.D(multiplexer_2_out), .clk(clock_1_out), .Q(d_ff_2_q));  // open: Qn, preset, reset
  assign controlled_buffer_4_out[2] = button_1_out ? d_ff_2_q : 1'bz;  // Controlled_Buffer controlled_buffer_2
  Hex_Digit_Display hex_digit_display_1 (.value(controlled_buffer_4_out));  // open: dp
  D_Flip_Flop d_ff_3 (.D(multiplexer_3_out), .clk(clock_1_out), .Q(d_ff_3_q));  // open: Qn, preset, reset
  Multiplexer #(.select(2)) multiplexer_3 (
    .in0(d_ff_3_q), .in1(d_ff_2_q), .in2(d_ff_4_q), .in3(in_4[1]), .out(multiplexer_3_out), .sel(in_3));
  assign controlled_buffer_4_out[1] = button_1_out ? d_ff_3_q : 1'bz;  // Controlled_Buffer controlled_buffer_3
  D_Flip_Flop d_ff_4 (.D(multiplexer_4_out), .clk(clock_1_out), .Q(d_ff_4_q));  // open: Qn, preset, reset
  Multiplexer #(.select(2)) multiplexer_4 (
    .in0(d_ff_4_q), .in1(d_ff_3_q), .in2(E), .in3(in_4[0]), .out(multiplexer_4_out), .sel(in_3));
  assign controlled_buffer_4_out[0] = button_1_out ? d_ff_4_q : 1'bz;  // Controlled_Buffer controlled_buffer_4
  LED SaiDir (.in(d_ff_4_q));
endmodule
