// Logisim project MUX8_1.circ as structural Verilog: 1 circuit, main circuit main
module main (
  input  A,
  input  B,
  input  C,
  input  D,
  output F,
  output out_6
);

  wire and_1_out, and_2_out, and_3_out, and_4_out, not_1_out, not_2_out, not_3_out, not_4_out, not_5_out;

  not not_1 (not_1_out, D);
  not not_2 (not_2_out, A);
  not not_3 (not_3_out, B);
  not not_4 (not_4_out, C);
  not not_5 (not_5_out, D);
  Multiplexer #(.select(3)) multiplexer_1 (
    .in0(D), .in1(D), .in2(1'b1), .in3(1'b0), .in4(D), .in5(not_1_out), .in6(1'b1), .in7(1'b0), .out(out_6),
    .sel({A, B, C}));
  and and_1 (and_1_out, not_2_out, not_3_out, D);
  and and_2 (and_2_out, B, not_4_out);
  and and_3 (and_3_out, not_4_out, D);
  and and_4 (and_4_out, A, not_3_out, C, not_5_out);
  or or_1 (F, and_1_out, and_2_out, and_3_out, and_4_out);
endmodule
