// Logisim project ProjetoContador.circ as structural Verilog: 1 circuit, main circuit main
module main (
  input  [1:0] in_1,
  input  [1:0] in_2,
  input  [1:0] in_3,
  output [1:0] out_4
);

  wire clock_1_out;
  wire [1:0] and_1_out, j_k_ff_2_q;

  assign and_1_out = in_2 & in_3;  // AND_Gate and_1, 2 bits wide
  Clock clock_1 (.out(clock_1_out));
  J_K_Flip_Flop j_k_ff_1 (
    .J(j_k_ff_2_q[0]), .K(j_k_ff_2_q[0]), .clk(clock_1_out), .Q(j_k_ff_2_q[1]));  // open: Qn, preset, reset
  Multiplexer #(.select(2), .width(2)) multiplexer_1 (
    .in0(in_1), .in1(and_1_out), .in2(2'b00), .in3(2'b11), .out(out_4), .sel(j_k_ff_2_q));
  J_K_Flip_Flop j_k_ff_2 (.J(1'b1), .K(1'b1), .clk(clock_1_out), .Q(j_k_ff_2_q[0]));  // open: Qn, preset, reset
endmodule
