// Logisim project ProjetoSomadorSub.circ as structural Verilog
module somadorcompleto (
  input  Cin,
  input  A,
  input  B,
  output S,
  output Cout
);

  wire meiosomador_1_cout, meiosomador_1_soma, meiosomador_2_cout;

  meiosomador meiosomador_1 (.B(B), .A(A), .Soma(meiosomador_1_soma), .Cout(meiosomador_1_cout));
  meiosomador meiosomador_2 (.B(meiosomador_1_soma), .A(Cin), .Soma(S), .Cout(meiosomador_2_cout));
  or or_1 (Cout, meiosomador_2_cout, meiosomador_1_cout);
endmodule

module meiosomador (
  input  A,
  input  B,
  output Soma,
  output Cout
);

  xor xor_1 (Soma, A, B);
  and and_1 (Cout, A, B);
endmodule

module Somador4bits (
  input  Co,
  input  A0,
  input  B0,
  input  A1,
  input  B1,
  input  A2,
  input  B2,
  input  A3,
  input  B3,
  output out_10,
  output out_11,
  output out_12,
  output out_13,
  output C4
);

  wire somadorcompleto_1_cout, somadorcompleto_2_cout, somadorcompleto_3_cout;

  somadorcompleto somadorcompleto_1 (.Cin(Co), .A(A0), .B(B0), .S(out_10), .Cout(somadorcompleto_1_cout));
  somadorcompleto somadorcompleto_2 (
    .Cin(somadorcompleto_1_cout), .A(A1), .B(B1), .S(out_11), .Cout(somadorcompleto_2_cout));
  somadorcompleto somadorcompleto_3 (
    .Cin(somadorcompleto_2_cout), .A(A2), .B(B2), .S(out_12), .Cout(somadorcompleto_3_cout));
  somadorcompleto somadorcompleto_4 (.Cin(somadorcompleto_3_cout), .A(A3), .B(B3), .S(out_13), .Cout(C4));
endmodule

module Somador8bits (
  input  C0,
  input  A0,
  input  B0,
  input  A1,
  input  B1,
  input  A2,
  input  B2,
  input  A3,
  input  B3,
  input  A4,
  input  B4,
  input  A5,
  input  B5,
  input  A6,
  input  B6,
  input  A7,
  input  B7,
  output out_18,
  output out_19,
  output out_20,
  output out_21,
  output out_22,
  output out_23,
  output out_24,
  output out_25
);

  wire somador4bits_1_c4, somador4bits_2_c4;

  Somador4bits somador4bits_1 (
    .Co(C0), .A0(A0), .B0(B0), .A1(A1), .B1(B1), .A2(A2), .B2(B2), .A3(A3), .B3(B3), .out_10(out_18),
    .out_11(out_19), .out_12(out_20), .out_13(out_21), .C4(somador4bits_1_c4));
  Somador4bits somador4bits_2 (
    .Co(somador4bits_1_c4), .A0(A4), .B0(B4), .A1(A5), .B1(B5), .A2(A6), .B2(B6), .A3(A7), .B3(B7),
    .out_10(out_22), .out_11(out_23), .out_12(out_24), .out_13(out_25), .C4(somador4bits_2_c4));
  LED led_1 (.in(somador4bits_2_c4));

  // Notes on the sheet:
  //   Estouro
  //   Somas menos sig.
  //   Somas mais sig.
endmodule

module SomadorSubtrador (
  input  Add_Sub_9ab186c8,
  input  A0,
  input  B0,
  input  A1,
  input  B1,
  input  A2,
  input  B2,
  input  A3,
  input  B3,
  output out_10,
  output out_11,
  output out_12,
  output out_13
);

  wire OVEFLOW_out, somadorcompleto_1_cout, somadorcompleto_2_cout, somadorcompleto_3_cout,
       somadorcompleto_4_cout, xor_1_out, xor_2_out, xor_3_out, xor_4_out;

  xor xor_1 (xor_1_out, B0, Add_Sub_9ab186c8);
  xor xor_2 (xor_2_out, B1, Add_Sub_9ab186c8);
  xor xor_3 (xor_3_out, B2, Add_Sub_9ab186c8);
  xor xor_4 (xor_4_out, B3, Add_Sub_9ab186c8);
  somadorcompleto somadorcompleto_1 (
    .Cin(Add_Sub_9ab186c8), .A(A0), .B(xor_1_out), .S(out_13), .Cout(somadorcompleto_1_cout));
  somadorcompleto somadorcompleto_2 (
    .Cin(somadorcompleto_1_cout), .A(A1), .B(xor_2_out), .S(out_12), .Cout(somadorcompleto_2_cout));
  somadorcompleto somadorcompleto_3 (
    .Cin(somadorcompleto_2_cout), .A(A2), .B(xor_3_out), .S(out_11), .Cout(somadorcompleto_3_cout));
  somadorcompleto somadorcompleto_4 (
    .Cin(somadorcompleto_3_cout), .A(A3), .B(xor_4_out), .S(out_10), .Cout(somadorcompleto_4_cout));
  or OVEFLOW (OVEFLOW_out, somadorcompleto_3_cout, somadorcompleto_4_cout);
  LED led_1 (.in(OVEFLOW_out));
endmodule
