// Logisim project Reg_Deslocamento.circ as structural Verilog: 1 circuit, main circuit main
module main (
  input  clear,
  input  shiftin,
  input  loadin,
  input  in_4,
  input  [7:0] in_5,
  input  LOAD,
  input  [7:0] in_7,
  input  SHIFT,
  input  Entrada
);

  wire clock_1_out, clock_2_out, shift_register_2_out, shift_register_3_p1;

  Clock clock_1 (.out(clock_1_out));
  // Shift_Register shift_register_1: pin names not known; wires that end beside it: clear, loadin, shiftin, clock_1_out, in_4, in_5[7], in_5[6], in_5[5], in_5[4], in_5[3], in_5[2], in_5[1], in_5[0]
  Shift_Register shift_register_2 (
    .shift(SHIFT), .in(Entrada), .clk(clock_2_out), .out(shift_register_2_out), .load(LOAD), .d0(in_7[7]),
    .d1(in_7[6]), .d2(in_7[5]), .d3(in_7[4]), .d4(in_7[3]), .d5(in_7[2]), .d6(in_7[1]), .d7(in_7[0]));  // open: clr, q0, q1, q2, q3, q4, q5, q6, q7
  Clock clock_2 (.out(clock_2_out));
  // Shift_Register shift_register_3: pin names not known; wires that end beside it: shift_register_3_p1, loadin, clock_1_out, shift_register_3_p1
  Shift_Register shift_register_4 (
    .in(shift_register_2_out), .clk(clock_2_out), .load(LOAD));  // open: shift, out, clr, d0, q0, d1, q1, d2, q2, d3, q3, d4, q4, d5, q5, d6, q6, d7, q7
endmodule
