// Logisim project Rel_Digital.circ as structural Verilog: 1 circuit, main circuit main
module main (
  input  [3:0] in_1
);

  wire and_1_out, CLK, counter_2_carry, counter_3_carry, counter_4_carry, counter_5_carry, counter_6_carry,
       d_ff_1_q, d_ff_2_q, d_ff_3_q, shift_register_1_out, shift_register_2_out;
  wire [3:0] Hor0, Hor1, Min0, Min1, Seg, Seg1;

  Hex_Digit_Display hex_digit_display_1 (.value(Hor0));  // open: dp
  Hex_Digit_Display #(.decimalPoint("false")) hex_digit_display_2 (.value(Hor1));
  Hex_Digit_Display #(.decimalPoint("false")) hex_digit_display_3 (.value(Min1));
  Hex_Digit_Display hex_digit_display_4 (.value(Min0));  // open: dp
  Hex_Digit_Display #(.decimalPoint("false")) hex_digit_display_5 (.value(Seg1));
  Hex_Digit_Display #(.decimalPoint("false")) hex_digit_display_6 (.value(Seg));
  Counter #(.max('h5), .width(4)) counter_1 (.D(in_1), .Q(Hor1), .clk(d_ff_1_q));  // open: load, count, carry, up, clr
  D_Flip_Flop d_ff_1 (.D(counter_2_carry), .clk(CLK), .Q(d_ff_1_q));  // open: Qn, preset, reset
  Counter #(.max('h9), .width(4)) counter_2 (
    .D(in_1), .Q(Hor0), .carry(counter_2_carry), .clk(d_ff_2_q));  // open: load, count, up, clr
  D_Flip_Flop d_ff_2 (.D(counter_3_carry), .clk(CLK), .Q(d_ff_2_q));  // open: Qn, preset, reset
  Clock clock_1 (.out(CLK));
  Counter #(.max('h5), .width(4)) counter_3 (
    .D(in_1), .Q(Min1), .carry(counter_3_carry), .clk(d_ff_3_q));  // open: load, count, up, clr
  Counter #(.max('h9), .width(4)) counter_4 (
    .D(in_1), .Q(Min0), .carry(counter_4_carry), .clk(shift_register_1_out));  // open: load, count, up, clr
  and and_1 (and_1_out, counter_4_carry, counter_5_carry, counter_6_carry);
  Shift_Register #(.length(10)) shift_register_1 (
    .in(counter_5_carry), .clk(CLK), .out(shift_register_1_out));  // open: shift, load, clr, d0, q0, d1, q1, d2, q2, d3, q3, d4, q4, d5, q5, d6, q6, d7, q7, d8, q8, d9, q9
  D_Flip_Flop d_ff_3 (.D(and_1_out), .clk(CLK), .Q(d_ff_3_q));  // open: Qn, preset, reset
  Counter #(.max('h5), .width(4)) counter_5 (
    .D(in_1), .Q(Seg1), .carry(counter_5_carry), .clk(shift_register_2_out));  // open: load, count, up, clr
  Shift_Register #(.length(1)) shift_register_2 (
    .in(counter_6_carry), .clk(CLK), .out(shift_register_2_out));  // open: shift, load, clr, d0, q0
  Counter #(.max('h9), .width(4)) counter_6 (
    .D(in_1), .Q(Seg), .carry(counter_6_carry), .clk(CLK));  // open: load, count, up, clr

  // Other names for the same wires on the sheet: zero[3:0] = in_1

  // Notes on the sheet:
  //   HORA - MINUTOS - SEGUNDOS
endmodule
