// Logisim project Acumulador_SAP1.circ as structural Verilog: 1 circuit, main circuit Acumulador
module Acumulador (
  input  in_1,
  input  in_2,
  input  in_3,
  input  in_4,
  input  in_5,
  input  in_6,
  input  in_7,
  input  in_8,
  input  in_9,
  input  in_10,
  input  in_11,
  input  CLR,
  output out_13,
  output out_14,
  output out_15,
  output out_16,
  output out_17,
  output out_18,
  output out_19,
  output out_20,
  output out_21,
  output out_22,
  output out_23,
  output out_24,
  output out_25,
  output out_26,
  output out_27,
  output out_28,
  output out_29,
  output out_30,
  output out_31,
  output out_32,
  output out_33,
  output out_34,
  output out_35,
  output out_36,
  output out_37,
  output out_38
);

  Register #(.width(4)) register_1 (
    .D({in_8, in_7, in_6, in_5}), .en(out_21), .Q({out_13, out_14, out_15, out_16}), .clk(in_10), .clr(CLR));
  assign {out_38, out_37, out_36, out_35} = in_11 ? {out_13, out_14, out_15, out_16} : 4'bz;  // Controlled_Buffer controlled_buffer_1
  Register #(.width(4)) register_2 (
    .D({in_4, in_3, in_2, in_1}), .en(out_21), .Q({out_17, out_18, out_19, out_20}), .clk(in_10), .clr(CLR));
  assign {out_34, out_33, out_32, out_31} = in_11 ? {out_17, out_18, out_19, out_20} : 4'bz;  // Controlled_Buffer controlled_buffer_2
  not not_1 (out_21, in_9);

  assign out_22 = in_11;
  assign out_23 = out_13;
  assign out_24 = out_14;
  assign out_25 = out_15;
  assign out_26 = out_16;
  assign out_27 = out_17;
  assign out_28 = out_18;
  assign out_29 = out_19;
  assign out_30 = out_20;

  // Other names for the same wires on the sheet: CLK = in_10; Ea = in_11; La = out_21
endmodule
