// Logisim project ControleSAP1.circ as structural Verilog: 11 circuits, main circuit SAPControler
module SAPControler (
  input  in_1,
  input  in_2,
  input  in_3,
  input  in_4,
  input  in_5,
  input  in_6,
  output out_7,
  output out_8,
  output out_9,
  output out_10,
  output out_11,
  output out_12,
  output out_13,
  output out_14,
  output out_15,
  output out_16,
  output out_17,
  output out_18,
  output Cp,
  output Ep,
  output Lm,
  output CE,
  output Li,
  output Ei,
  output La,
  output Ea,
  output Su,
  output Eu,
  output Lb,
  output Lo,
  output out_31
);

  wire and_1_out, and_2_out, and_3_out, j_k_ff_1_qn, j_k_ff_2_qn, j_k_ff_3_qn, j_k_ff_4_qn, j_k_ff_5_qn,
       j_k_ff_6_q, nand_1_out, or_1_out, or_2_out, undriven;

  Inst_Decoder inst_decoder_1 (
    .in_1(in_1), .in_2(in_2), .in_3(in_3), .in_4(in_4), .out_5(out_14), .out_6(out_15), .out_7(out_16),
    .out_8(out_17), .out_9(out_18));
  Lm_Logic lm_logic_1 (.in_1(Ep), .in_2(out_14), .in_3(out_15), .in_4(out_16), .in_5(out_10), .out_6(Lm));
  J_K_Flip_Flop #(.trigger("falling")) j_k_ff_1 (
    .J(out_9), .clk(in_5), .K(j_k_ff_2_qn), .Q(out_8), .Qn(j_k_ff_1_qn), .reset(in_6));  // open: preset, en
  CE_Logic ce_logic_1 (.in_1(out_11), .in_2(out_14), .in_3(out_15), .in_4(out_16), .in_5(out_9), .out_6(CE));
  not not_1 (Li, out_11);
  J_K_Flip_Flop #(.trigger("falling")) j_k_ff_2 (
    .J(out_10), .clk(in_5), .K(j_k_ff_3_qn), .Q(out_9), .Qn(j_k_ff_2_qn), .reset(in_6));  // open: preset, en
  Ei_Logic ei_logic_1 (.in_1(out_14), .in_2(out_15), .in_3(out_16), .in_4(out_10), .out_5(Ei));
  J_K_Flip_Flop #(.trigger("falling")) j_k_ff_3 (
    .J(out_11), .clk(in_5), .K(j_k_ff_4_qn), .Q(out_10), .Qn(j_k_ff_3_qn), .reset(in_6));  // open: preset, en
  La_Logic la_logic_1 (.in_1(out_14), .in_2(out_9), .in_3(out_15), .in_4(out_16), .in_5(out_8), .out_6(La));
  J_K_Flip_Flop #(.trigger("falling")) j_k_ff_4 (
    .J(Cp), .clk(in_5), .K(j_k_ff_5_qn), .Q(out_11), .Qn(j_k_ff_4_qn), .reset(in_6));  // open: preset, en
  J_K_Flip_Flop #(.trigger("falling")) j_k_ff_5 (
    .J(Ep), .clk(in_5), .K(j_k_ff_6_q), .Q(Cp), .Qn(j_k_ff_5_qn), .preset(undriven), .en(undriven),
    .reset(in_6));
  Ea_Logic ea_logic_1 (.in_1(out_17), .in_2(out_10), .out_3(Ea));
  J_K_Flip_Flop #(.trigger("falling")) j_k_ff_6 (
    .J(j_k_ff_1_qn), .clk(in_5), .K(out_8), .Q(j_k_ff_6_q), .Qn(Ep), .reset(in_6));  // open: preset, en
  Su_Logic su_logic_1 (.in_1(out_16), .in_2(out_8), .out_3(Su));
  Eu_Logic eu_logic_1 (.in_1(out_15), .in_2(out_16), .in_3(out_8), .out_4(Eu));
  Lb_Logic lb_logic_1 (.in_1(out_15), .in_2(out_16), .in_3(out_9), .out_4(Lb));
  Lo_Logic lo_logic_1 (.in_1(out_17), .in_2(out_10), .out_3(Lo));
  or or_1 (or_1_out, out_8, out_9);
  nand nand_1 (nand_1_out, ~Cp, ~Ep, Lm, CE, Li, Ei, La, ~Ea, ~Su, ~Eu, Lb, Lo);  // NAND_Gate
  and and_1 (and_1_out, or_1_out, or_2_out);
  or or_2 (or_2_out, out_16, out_15);
  not not_2 (out_31, nand_1_out);
  or or_3 (out_7, and_1_out, and_3_out, and_2_out);
  and and_2 (and_2_out, out_9, out_14);
  and and_3 (and_3_out, out_17, out_10);

  assign out_12 = Cp;
  assign out_13 = Ep;

  // Other names for the same wires on the sheet: ADD = out_15; LDA = out_14; nHLT = out_18; OUT = out_17;
  //   SUB = out_16; T1 = Ep; T2 = Cp; T3 = out_11; T4 = out_10; T5 = out_9; T6 = out_8
endmodule

module Inst_Decoder (
  input  in_1,
  input  in_2,
  input  in_3,
  input  in_4,
  output out_5,
  output out_6,
  output out_7,
  output out_8,
  output out_9
);

  wire not_1_out, not_2_out, not_3_out, not_4_out;

  not not_1 (not_1_out, in_1);
  not not_2 (not_2_out, in_3);
  not not_3 (not_3_out, in_2);
  not not_4 (not_4_out, in_4);
  and and_1 (out_5, not_1_out, not_3_out, not_2_out, not_4_out);
  and and_2 (out_6, not_1_out, not_3_out, not_2_out, in_4);
  and and_3 (out_7, not_1_out, not_3_out, in_3, not_4_out);
  and and_4 (out_8, in_1, in_2, in_3, not_4_out);
  and and_5 (out_9, in_1, in_2, in_3, in_4);
endmodule

module Lm_Logic (
  input  in_1,
  input  in_2,
  input  in_3,
  input  in_4,
  input  in_5,
  output out_6
);

  wire and_1_out, and_2_out, and_3_out, or_1_out;

  and and_1 (and_1_out, in_2, in_5);
  or or_1 (or_1_out, in_1, and_1_out, and_2_out, and_3_out);
  not not_1 (out_6, or_1_out);
  and and_2 (and_2_out, in_3, in_5);
  and and_3 (and_3_out, in_4, in_5);
endmodule

module CE_Logic (
  input  in_1,
  input  in_2,
  input  in_3,
  input  in_4,
  input  in_5,
  output out_6
);

  wire and_1_out, and_2_out, and_3_out, or_1_out;

  and and_1 (and_1_out, in_2, in_5);
  or or_1 (or_1_out, in_1, and_1_out, and_2_out, and_3_out);
  not not_1 (out_6, or_1_out);
  and and_2 (and_2_out, in_3, in_5);
  and and_3 (and_3_out, in_4, in_5);
endmodule

module Ei_Logic (
  input  in_1,
  input  in_2,
  input  in_3,
  input  in_4,
  output out_5
);

  wire and_1_out, and_2_out, and_3_out, or_1_out;

  and and_1 (and_1_out, in_1, in_4);
  or or_1 (or_1_out, and_1_out, and_2_out, and_3_out);
  not not_1 (out_5, or_1_out);
  and and_2 (and_2_out, in_2, in_4);
  and and_3 (and_3_out, in_3, in_4);
endmodule

module La_Logic (
  input  in_1,
  input  in_2,
  input  in_3,
  input  in_4,
  input  in_5,
  output out_6
);

  wire and_1_out, and_2_out, and_3_out, or_1_out;

  and and_1 (and_1_out, in_1, in_2);
  or or_1 (or_1_out, and_1_out, and_2_out, and_3_out);
  not not_1 (out_6, or_1_out);
  and and_2 (and_2_out, in_3, in_5);
  and and_3 (and_3_out, in_4, in_5);
endmodule

module Ea_Logic (
  input  in_1,
  input  in_2,
  output out_3
);

  and and_1 (out_3, in_1, in_2);
endmodule

module Su_Logic (
  input  in_1,
  input  in_2,
  output out_3
);

  and and_1 (out_3, in_1, in_2);
endmodule

module Eu_Logic (
  input  in_1,
  input  in_2,
  input  in_3,
  output out_4
);

  wire and_1_out, and_2_out;

  and and_1 (and_1_out, in_1, in_3);
  and and_2 (and_2_out, in_2, in_3);
  or or_1 (out_4, and_1_out, and_2_out);
endmodule

module Lb_Logic (
  input  in_1,
  input  in_2,
  input  in_3,
  output out_4
);

  wire and_1_out, and_2_out, or_1_out;

  and and_1 (and_1_out, in_1, in_3);
  and and_2 (and_2_out, in_2, in_3);
  or or_1 (or_1_out, and_1_out, and_2_out);
  not not_1 (out_4, or_1_out);
endmodule

module Lo_Logic (
  input  in_1,
  input  in_2,
  output out_3
);

  nand nand_1 (out_3, in_1, in_2);
endmodule
