// Logisim project PC_SAP1.circ as structural Verilog: 1 circuit, main circuit PC
module PC (
  input  Cp,
  input  nCLK,
  input  Clear,
  input  in_4,
  output indicador_de_atividade,
  output out_6,
  output out_7,
  output out_8,
  output out_9
);

  wire j_k_ff_1_q, j_k_ff_2_q, j_k_ff_3_q, j_k_ff_4_q;

  J_K_Flip_Flop #(.trigger("falling")) j_k_ff_1 (
    .J(Cp), .clk(nCLK), .K(Cp), .Q(j_k_ff_1_q), .reset(Clear));  // open: Qn, preset, en
  assign out_6 = in_4 ? j_k_ff_1_q : 1'bz;  // Controlled_Buffer controlled_buffer_1
  J_K_Flip_Flop #(.trigger("falling")) j_k_ff_2 (
    .J(Cp), .clk(j_k_ff_1_q), .K(Cp), .Q(j_k_ff_2_q), .reset(Clear));  // open: Qn, preset, en
  assign out_7 = in_4 ? j_k_ff_2_q : 1'bz;  // Controlled_Buffer controlled_buffer_2
  J_K_Flip_Flop #(.trigger("falling")) j_k_ff_3 (
    .J(Cp), .clk(j_k_ff_2_q), .K(Cp), .Q(j_k_ff_3_q), .reset(Clear));  // open: Qn, preset, en
  assign out_8 = in_4 ? j_k_ff_3_q : 1'bz;  // Controlled_Buffer controlled_buffer_3
  J_K_Flip_Flop #(.trigger("falling")) j_k_ff_4 (
    .J(Cp), .clk(j_k_ff_3_q), .K(Cp), .Q(j_k_ff_4_q), .reset(Clear));  // open: Qn, preset, en
  assign out_9 = in_4 ? j_k_ff_4_q : 1'bz;  // Controlled_Buffer controlled_buffer_4
  or or_1 (indicador_de_atividade, Cp, in_4);

  // Other names for the same wires on the sheet: Ep = in_4
endmodule
