// Logisim project RegistradorDeSaida_SAP1.circ as structural Verilog: 1 circuit, main circuit REG_Saida
module REG_Saida (
  input  in_1,
  input  in_2,
  input  in_3,
  input  in_4,
  input  in_5,
  input  in_6,
  input  in_7,
  input  in_8,
  input  in_9,
  input  in_10,
  input  in_11,
  output out_12,
  output out_13,
  output out_14,
  output out_15,
  output out_16,
  output out_17,
  output out_18,
  output out_19,
  output out_20
);

  Register #(.width(4)) register_1 (
    .D({in_8, in_7, in_6, in_5}), .en(out_20), .Q({out_12, out_13, out_14, out_15}), .clk(in_11), .clr(in_9));
  Register #(.width(4)) register_2 (
    .D({in_4, in_3, in_2, in_1}), .en(out_20), .Q({out_16, out_17, out_18, out_19}), .clk(in_11), .clr(in_9));
  not not_1 (out_20, in_10);

  // Other names for the same wires on the sheet: CLK = in_11; CLR = in_9; Lo = out_20
endmodule
