// Logisim project SAP1_Computer_OK.circ as structural Verilog: 1 circuit, main circuit Montagem_SAP1
// ~HLT
module Montagem_SAP1 (
  input  in_1,
  input  [3:0] \Endereço ,
  input  [7:0] in_3,
  input  Run_1__Prog_0,
  input  CLR_MEM,
  output out_6,
  output out_7,
  output out_8,
  output out_9,
  output out_10,
  output out_11,
  output out_12,
  output out_13
);

  wire acumulador_1_out_13, acumulador_1_out_14, acumulador_1_out_15, acumulador_1_out_16,
       acumulador_1_out_17, acumulador_1_out_18, acumulador_1_out_19, acumulador_1_out_20,
       acumulador_1_out_21, acumulador_1_out_22, acumulador_1_out_23, acumulador_1_out_24,
       acumulador_1_out_25, acumulador_1_out_26, acumulador_1_out_27, acumulador_1_out_28,
       acumulador_1_out_29, acumulador_1_out_30, button_1_out, CLK, clock_1_out, Cp, Ea, Ep, Eu, HLT,
       mar_1_indicador_de_atividade, mar_1_out_9, mar_1_out_10, mar_1_out_11, mar_1_out_12,
       multiplexer_1_out, nCE, nCLK, nEi, nLa, nLb, nLi, nLm, nLo, not_1_out, pc_1_indicador_de_atividade,
       pc_1_out_6, pc_1_out_7, pc_1_out_8, pc_1_out_9, ram_16_x_8_1_mostrador_de_atividade,
       ram_16_x_8_1_out_13, ram_16_x_8_1_out_16, ram_16_x_8_1_out_17, ram_16_x_8_1_out_18,
       ram_16_x_8_1_out_19, reg_b_1_indicador_de_atividade, reg_b_1_out_12, reg_b_1_out_13, reg_b_1_out_14,
       reg_b_1_out_15, reg_b_1_out_16, reg_b_1_out_17, reg_b_1_out_18, reg_b_1_out_19, reg_saida_1_out_20,
       ri_1_out_14, ri_1_out_15, ri_1_out_16, ri_1_out_17, ri_1_out_18, sapcontroler_1_out_7,
       sapcontroler_1_out_8, sapcontroler_1_out_9, sapcontroler_1_out_10, sapcontroler_1_out_11,
       sapcontroler_1_out_12, sapcontroler_1_out_13, sapcontroler_1_out_14, sapcontroler_1_out_15,
       sapcontroler_1_out_16, sapcontroler_1_out_17, sapcontroler_1_out_31, Su,
       ula_1_indicador_de_atividade__eu, ula_1_indicador_de_operacao, ula_1_vai_para_o_reg_b;

  Multiplexer #(.enable("false")) multiplexer_1 (.in0(1'b0), .in1(nCE), .out(multiplexer_1_out), .sel(Run_1__Prog_0));
  Button button_1 (.out(button_1_out));
  DotMatrix #(.matrixcols(3), .matrixrows(1)) dotmatrix_1 (
    .col0(sapcontroler_1_out_8), .col1(sapcontroler_1_out_9), .col2(sapcontroler_1_out_10));
  PC pc_1 (
    .Cp(Cp), .nCLK(nCLK), .Clear(in_1), .in_4(Ep), .out_6(pc_1_out_6), .out_7(pc_1_out_7),
    .out_8(pc_1_out_8), .out_9(pc_1_out_9), .indicador_de_atividade(pc_1_indicador_de_atividade));
  DotMatrix #(.matrixcols(1), .matrixrows(1)) dotmatrix_2 (.col0(pc_1_indicador_de_atividade));
  MAR mar_1 (
    .nLm(nLm), .CLK(CLK), .in_1(pc_1_out_9), .in_2(pc_1_out_8), .in_3(pc_1_out_7), .in_5(pc_1_out_6),
    .indicador_de_atividade(mar_1_indicador_de_atividade), .out_9(mar_1_out_9), .out_10(mar_1_out_10),
    .out_11(mar_1_out_11), .out_12(mar_1_out_12), .vem_da_RAM__CE(ram_16_x_8_1_out_13));
  DotMatrix #(.inputtype("row"), .matrixcols(1), .matrixrows(1)) dotmatrix_3 (.row0(mar_1_indicador_de_atividade));
  RAM_16_X_8 ram_16_x_8_1 (
    .CE(multiplexer_1_out), .WE(button_1_out), .in_9(\Endereço ), .in_10(in_3), .out_11(pc_1_out_6),
    .out_12(pc_1_out_7), .out_14(pc_1_out_8), .out_15(pc_1_out_9), .out_16(ram_16_x_8_1_out_16),
    .out_17(ram_16_x_8_1_out_17), .out_18(ram_16_x_8_1_out_18), .out_19(ram_16_x_8_1_out_19),
    .in_1(mar_1_out_9), .Addr__from_PC(mar_1_out_10), .in_3(mar_1_out_11), .in_4(mar_1_out_12),
    .Run_1__Prog_0(Run_1__Prog_0), .in_8(CLR_MEM),
    .mostrador_de_atividade(ram_16_x_8_1_mostrador_de_atividade), .out_13(ram_16_x_8_1_out_13));
  DotMatrix #(.inputtype("row"), .matrixcols(1), .matrixrows(1)) dotmatrix_4 (.row0(ram_16_x_8_1_mostrador_de_atividade));
  RI ri_1 (
    .Li(nLi), .CLK(CLK), .CLR(in_1), .Ei(nEi), .in_1(ram_16_x_8_1_out_19), .in_2(ram_16_x_8_1_out_18),
    .in_3(ram_16_x_8_1_out_17), .in_5(ram_16_x_8_1_out_16), .in_7(pc_1_out_9), .in_9(pc_1_out_8),
    .in_10(pc_1_out_7), .in_11(pc_1_out_6), .out_19(pc_1_out_6), .out_20(pc_1_out_7), .out_21(pc_1_out_8),
    .out_22(pc_1_out_9), .out_14(ri_1_out_14), .out_15(ri_1_out_15), .out_16(ri_1_out_16),
    .out_17(ri_1_out_17), .out_18(ri_1_out_18), .in_13(sapcontroler_1_out_7));
  DotMatrix #(.inputtype("row"), .matrixcols(1), .matrixrows(1)) dotmatrix_5 (.row0(ri_1_out_14));
  DotMatrix #(.matrixcols(3), .matrixrows(1)) dotmatrix_6 (
    .col0(sapcontroler_1_out_11), .col1(sapcontroler_1_out_12), .col2(sapcontroler_1_out_13));
  DotMatrix #(.matrixcols(4), .matrixrows(1)) dotmatrix_7 (
    .col0(sapcontroler_1_out_14), .col1(sapcontroler_1_out_15), .col2(sapcontroler_1_out_16),
    .col3(sapcontroler_1_out_17));
  SAPControler sapcontroler_1 (
    .in_5(CLK), .out_18(HLT), .in_1(ri_1_out_15), .in_2(ri_1_out_16), .in_3(ri_1_out_17), .in_4(ri_1_out_18),
    .Cp(Cp), .Ep(Ep), .Lm(nLm), .CE(nCE), .Li(nLi), .Ei(nEi), .La(nLa), .Ea(Ea), .Su(Su), .Eu(Eu), .Lb(nLb),
    .Lo(nLo), .out_13(sapcontroler_1_out_13), .out_12(sapcontroler_1_out_12), .out_11(sapcontroler_1_out_11),
    .out_10(sapcontroler_1_out_10), .out_9(sapcontroler_1_out_9), .out_8(sapcontroler_1_out_8),
    .out_31(sapcontroler_1_out_31), .out_14(sapcontroler_1_out_14), .out_15(sapcontroler_1_out_15),
    .out_16(sapcontroler_1_out_16), .out_17(sapcontroler_1_out_17), .in_6(in_1), .out_7(sapcontroler_1_out_7));
  LED NOP (.in(sapcontroler_1_out_31));
  DotMatrix #(.inputtype("row"), .matrixcols(1), .matrixrows(8)) dotmatrix_8 (
    .row0(pc_1_out_6), .row1(pc_1_out_7), .row2(pc_1_out_8), .row3(pc_1_out_9), .row4(ram_16_x_8_1_out_16),
    .row5(ram_16_x_8_1_out_17), .row6(ram_16_x_8_1_out_18), .row7(ram_16_x_8_1_out_19));
  DotMatrix #(.matrixcols(8), .matrixrows(1), .dotshape("circle")) dotmatrix_9 (
    .col0(acumulador_1_out_13), .col1(acumulador_1_out_14), .col2(acumulador_1_out_15),
    .col3(acumulador_1_out_16), .col4(acumulador_1_out_17), .col5(acumulador_1_out_18),
    .col6(acumulador_1_out_19), .col7(acumulador_1_out_20));
  DotMatrix #(.matrixcols(1), .matrixrows(1)) dotmatrix_10 (.col0(acumulador_1_out_21));
  DotMatrix #(.matrixcols(1), .matrixrows(1)) dotmatrix_11 (.col0(acumulador_1_out_22));
  DotMatrix #(.inputtype("row"), .matrixcols(1), .matrixrows(1)) dotmatrix_12 (.row0(ula_1_indicador_de_operacao));
  DotMatrix #(.inputtype("row"), .matrixcols(1), .matrixrows(1)) dotmatrix_13 (.row0(ula_1_indicador_de_atividade__eu));
  DotMatrix #(.inputtype("row"), .matrixcols(1), .matrixrows(1)) dotmatrix_14 (.row0(reg_b_1_indicador_de_atividade));
  DotMatrix #(.inputtype("row"), .matrixcols(1), .matrixrows(1)) dotmatrix_15 (.row0(reg_saida_1_out_20));
  Acumulador acumulador_1 (
    .in_1(pc_1_out_6), .in_2(pc_1_out_7), .in_3(pc_1_out_8), .in_4(pc_1_out_9), .in_5(ram_16_x_8_1_out_16),
    .in_6(ram_16_x_8_1_out_17), .in_7(ram_16_x_8_1_out_18), .in_8(ram_16_x_8_1_out_19), .out_31(pc_1_out_6),
    .out_32(pc_1_out_7), .out_33(pc_1_out_8), .out_34(pc_1_out_9), .out_35(ram_16_x_8_1_out_16),
    .out_36(ram_16_x_8_1_out_17), .out_37(ram_16_x_8_1_out_18), .out_38(ram_16_x_8_1_out_19), .in_9(nLa),
    .in_10(CLK), .in_11(Ea), .out_21(acumulador_1_out_21), .out_22(acumulador_1_out_22),
    .out_23(acumulador_1_out_23), .out_24(acumulador_1_out_24), .out_25(acumulador_1_out_25),
    .out_26(acumulador_1_out_26), .out_27(acumulador_1_out_27), .out_28(acumulador_1_out_28),
    .out_29(acumulador_1_out_29), .out_30(acumulador_1_out_30), .out_13(acumulador_1_out_13),
    .out_14(acumulador_1_out_14), .out_15(acumulador_1_out_15), .out_16(acumulador_1_out_16),
    .out_17(acumulador_1_out_17), .out_18(acumulador_1_out_18), .out_19(acumulador_1_out_19),
    .out_20(acumulador_1_out_20), .CLR(in_1));
  ULA ula_1 (
    .out_19(ram_16_x_8_1_out_19), .out_21(ram_16_x_8_1_out_18), .out_22(ram_16_x_8_1_out_17),
    .out_23(ram_16_x_8_1_out_16), .out_24(pc_1_out_9), .out_25(pc_1_out_8), .out_26(pc_1_out_7),
    .out_27(pc_1_out_6), .Su(Su), .in_18(Eu), .indicador_de_atividade__Eu(ula_1_indicador_de_atividade__eu),
    .in_1(acumulador_1_out_23), .in_2(acumulador_1_out_24), .in_3(acumulador_1_out_25),
    .in_4(acumulador_1_out_26), .in_5(acumulador_1_out_27), .in_6(acumulador_1_out_28),
    .in_7(acumulador_1_out_29), .in_8(acumulador_1_out_30),
    .indicador_de_operacao(ula_1_indicador_de_operacao), .in_10(reg_b_1_out_12), .in_11(reg_b_1_out_13),
    .in_12(reg_b_1_out_14), .in_13(reg_b_1_out_15), .in_14(reg_b_1_out_16), .in_15(reg_b_1_out_17),
    .in_16(reg_b_1_out_18), .in_17(reg_b_1_out_19), .vai_para_o_Reg_B(ula_1_vai_para_o_reg_b));
  REG_B reg_b_1 (
    .in_1(pc_1_out_6), .in_2(pc_1_out_7), .in_3(pc_1_out_8), .in_4(pc_1_out_9), .in_5(ram_16_x_8_1_out_16),
    .in_6(ram_16_x_8_1_out_17), .in_7(ram_16_x_8_1_out_18), .in_8(ram_16_x_8_1_out_19), .in_9(nLb),
    .in_10(CLK), .out_12(reg_b_1_out_12), .out_13(reg_b_1_out_13), .out_14(reg_b_1_out_14),
    .out_15(reg_b_1_out_15), .out_16(reg_b_1_out_16), .out_17(reg_b_1_out_17), .out_18(reg_b_1_out_18),
    .out_19(reg_b_1_out_19), .indicador_de_atividade(reg_b_1_indicador_de_atividade),
    .vem_da_ULA__Eu(ula_1_vai_para_o_reg_b));
  REG_Saida reg_saida_1 (
    .in_1(pc_1_out_6), .in_2(pc_1_out_7), .in_3(pc_1_out_8), .in_4(pc_1_out_9), .in_5(ram_16_x_8_1_out_16),
    .in_6(ram_16_x_8_1_out_17), .in_7(ram_16_x_8_1_out_18), .in_8(ram_16_x_8_1_out_19), .in_10(nLo),
    .in_11(CLK), .out_12(out_6), .out_13(out_7), .out_14(out_8), .out_15(out_9), .out_16(out_10),
    .out_17(out_11), .out_18(out_12), .out_19(out_13), .in_9(in_1), .out_20(reg_saida_1_out_20));
  Clock clock_1 (.out(clock_1_out));
  not not_1 (not_1_out, clock_1_out);
  Multiplexer #(.enable("false")) multiplexer_2 (.in0(not_1_out), .in1(1'b0), .out(nCLK), .sel(HLT));
  Multiplexer #(.enable("false")) multiplexer_3 (.in0(clock_1_out), .in1(1'b0), .out(CLK), .sel(HLT));

  // Other names for the same wires on the sheet: CLR = in_1; Run_Prog = Run_1__Prog_0

  // Notes on the sheet:
  //   Dados
  //   WE
  //   T6T5T4
  //   →
  //   PC
  //   REM
  //   ←
  //   ↓
  //   →
  //   RAM
  //   ←
  //   ↓
  //   →
  //   ↓
  //   RI
  //   T3T2T1
  //   LDA ADD SUB OUT
  //   BUS W
  //   ┐
  //   →
  //   ↓
  //   ←
  //   ↓
  //   AC
  //   SUB
  //   ↑
  //   ←
  //   ULA
  //   ↑
  //   →
  //   RB
  //   →
  //   ↓
  //   RS
endmodule
