// Logisim project ULA_SAP1.circ as structural Verilog: 1 circuit, main circuit ULA
module ULA (
  input  in_1,
  input  in_2,
  input  in_3,
  input  in_4,
  input  in_5,
  input  in_6,
  input  in_7,
  input  in_8,
  input  Su,
  input  in_10,
  input  in_11,
  input  in_12,
  input  in_13,
  input  in_14,
  input  in_15,
  input  in_16,
  input  in_17,
  input  in_18,
  output out_19,
  output indicador_de_operacao,
  output out_21,
  output out_22,
  output out_23,
  output out_24,
  output out_25,
  output out_26,
  output out_27,
  output indicador_de_atividade__Eu,
  output vai_para_o_Reg_B
);

  wire Cout_0;
  wire [3:0] Nibble_0, Nibble_1, xor_4_out, xor_8_out;

  assign {out_19, out_21, out_22, out_23} = in_18 ? Nibble_1 : 4'bz;  // Controlled_Buffer controlled_buffer_1
  assign {out_24, out_25, out_26, out_27} = in_18 ? Nibble_0 : 4'bz;  // Controlled_Buffer controlled_buffer_2
  xor xor_1 (xor_4_out[3], in_10, Su);
  xor xor_2 (xor_4_out[2], in_11, Su);
  Adder #(.width(4)) adder_1 (.a({in_1, in_2, in_3, in_4}), .b(xor_4_out), .out(Nibble_1), .cin(Cout_0));  // open: cout
  xor xor_3 (xor_4_out[1], in_12, Su);
  xor xor_4 (xor_4_out[0], in_13, Su);
  xor xor_5 (xor_8_out[3], in_14, Su);
  xor xor_6 (xor_8_out[2], in_15, Su);
  Adder #(.width(4)) adder_2 (.a({in_5, in_6, in_7, in_8}), .b(xor_8_out), .out(Nibble_0), .cin(Su), .cout(Cout_0));
  xor xor_7 (xor_8_out[1], in_16, Su);
  xor xor_8 (xor_8_out[0], in_17, Su);

  assign indicador_de_atividade__Eu = in_18;
  assign indicador_de_operacao = Su;
  assign vai_para_o_Reg_B = in_18;

  // Other names for the same wires on the sheet: Eu = in_18
endmodule
