// Logisim project Sequencial.circ as structural Verilog: 1 circuit, main circuit main
module main (
  input  in_1,
  input  in_2,
  input  in_3,
  input  in_4,
  input  in_5
);

  wire and_1_out, and_2_out, nand_1_out, nand_2_out, nor_1_out, nor_2_out, nor_3_out, nor_4_out;

  nand nand_1 (nand_1_out, in_1, nand_2_out);
  nand nand_2 (nand_2_out, nand_1_out, in_3);
  nor nor_1 (nor_1_out, in_1, nor_2_out);
  nor nor_2 (nor_2_out, in_3, nor_1_out);
  LED led_1 (.in(nor_1_out));
  LED led_2 (.in(nor_2_out));
  LED led_3 (.in(nand_1_out));
  LED led_4 (.in(nand_2_out));
  and and_1 (and_1_out, in_2, in_4);
  and and_2 (and_2_out, in_4, in_5);
  nor nor_3 (nor_3_out, and_1_out, nor_4_out);
  nor nor_4 (nor_4_out, nor_3_out, and_2_out);
  LED led_5 (.in(nor_3_out));
  LED led_6 (.in(nor_4_out));
endmodule
