// Logisim project TECLADO.circ as structural Verilog: 2 circuits, main circuit main
module main (
  input  in_1,
  input  F,
  input  K,
  input  P,
  input  U,
  input  Z,
  input  A,
  input  B,
  input  G,
  input  L,
  input  Q,
  input  V,
  input  SPC,
  input  H,
  input  M,
  input  R,
  input  W,
  input  C,
  input  D,
  input  I,
  input  N,
  input  S,
  input  X,
  input  E,
  input  J,
  input  O,
  input  T,
  input  Y,
  output [7:0] out_29,
  output [7:0] out_30
);

  wire clock_1_out, clock_2_out;
  wire [6:0] DADOS;
  wire [7:0] register_1_q;

  assign out_29 = A ? {8{1'b0}} : 8'bz;  // Controlled_Buffer controlled_buffer_1
  assign out_29 = B ? 8'h1 : 8'bz;  // Controlled_Buffer controlled_buffer_2
  assign out_29 = C ? 8'h2 : 8'bz;  // Controlled_Buffer controlled_buffer_3
  assign out_29 = D ? 8'h3 : 8'bz;  // Controlled_Buffer controlled_buffer_4
  assign out_29 = E ? 8'h4 : 8'bz;  // Controlled_Buffer controlled_buffer_5
  assign out_29 = F ? 8'h5 : 8'bz;  // Controlled_Buffer controlled_buffer_6
  assign out_29 = G ? 8'h6 : 8'bz;  // Controlled_Buffer controlled_buffer_7
  assign out_29 = H ? 8'h7 : 8'bz;  // Controlled_Buffer controlled_buffer_8
  Controlled_Buffer controlled_buffer_9 (.in(H), .en(H));  // open: out
  assign out_29 = I ? 8'h8 : 8'bz;  // Controlled_Buffer controlled_buffer_10
  assign out_29 = J ? 8'h9 : 8'bz;  // Controlled_Buffer controlled_buffer_11
  assign out_29 = K ? 8'ha : 8'bz;  // Controlled_Buffer controlled_buffer_12
  assign out_29 = L ? 8'hb : 8'bz;  // Controlled_Buffer controlled_buffer_13
  assign out_29 = M ? 8'hc : 8'bz;  // Controlled_Buffer controlled_buffer_14
  assign out_29 = N ? 8'hd : 8'bz;  // Controlled_Buffer controlled_buffer_15
  assign out_29 = O ? 8'he : 8'bz;  // Controlled_Buffer controlled_buffer_16
  assign out_29 = P ? 8'hf : 8'bz;  // Controlled_Buffer controlled_buffer_17
  assign out_29 = Q ? 8'h10 : 8'bz;  // Controlled_Buffer controlled_buffer_18
  assign out_29 = R ? 8'h11 : 8'bz;  // Controlled_Buffer controlled_buffer_19
  assign out_29 = S ? 8'h12 : 8'bz;  // Controlled_Buffer controlled_buffer_20
  assign out_29 = T ? 8'h13 : 8'bz;  // Controlled_Buffer controlled_buffer_21
  assign out_29 = U ? 8'h14 : 8'bz;  // Controlled_Buffer controlled_buffer_22
  assign out_29 = V ? 8'h15 : 8'bz;  // Controlled_Buffer controlled_buffer_23
  assign out_29 = W ? 8'h16 : 8'bz;  // Controlled_Buffer controlled_buffer_24
  assign out_29 = X ? 8'h17 : 8'bz;  // Controlled_Buffer controlled_buffer_25
  assign out_29 = Y ? 8'h18 : 8'bz;  // Controlled_Buffer controlled_buffer_26
  ROM #(.misaligned("true")) rom_1 (.addr(out_29), .data(out_30));
  assign out_29 = Z ? 8'h19 : 8'bz;  // Controlled_Buffer controlled_buffer_27
  assign out_29 = SPC ? 8'h1a : 8'bz;  // Controlled_Buffer controlled_buffer_28
  Clock clock_1 (.out(clock_1_out));
  TTY tty_1 (.data(DADOS), .clk(clock_1_out), .we(in_1));  // open: clr
  Register register_1 (.D(out_30), .en(in_1), .clk(clock_2_out), .Q(register_1_q));  // open: clr
  Clock clock_2 (.out(clock_2_out));
  Bit_Extender #(.out_width(7)) bit_extender_1 (.in(register_1_q), .out(DADOS));

  // Other names for the same wires on the sheet: REF[7:0] = out_29; WRT = in_1

  // Notes on the sheet:
  //   contents of rom_1 (hex, n*v repeats v):
  //   41 42 43 44 45 46 47 48 49 4a 4b 4c 4d 4e 4f 50 51 52 53 54 55 56 57 58 59 5a 20
endmodule

module circ (
);

  wire A, B, C, CLK, CLR, ESPACO, F, I, K, L, N, O, Q, R, SEL, T, U, W, X, Z;
  wire [6:0] DADOS;
  wire [7:0] REF, register_1_q, rom_1_data;

  main main_1 (
    .B(A), .C(A), .D(A), .F(A), .G(A), .H(A), .I(A), .J(A), .K(A), .L(A), .M(A), .N(A), .O(A), .P(A), .S(A),
    .V(A), .X(A), .Z(A), .SPC(A), .out_29(REF));  // open: A, E, in_1, Q, R, T, U, W, Y, out_30
  Clock clock_1 (.out(CLK));
  ROM rom_1 (.addr(REF), .data(rom_1_data));
  Button button_1 (.out(Q));
  Button button_2 (.out(W));
  Button button_3 (.out(A));
  Button button_4 (.out(Z));
  Button button_5 (.out(A));
  Button button_6 (.out(R));
  Button button_7 (.out(A));
  Button button_8 (.out(A));
  Button button_9 (.out(X));
  Button button_10 (.out(C));
  Button button_11 (.out(T));
  Button button_12 (.out(A));
  Button button_13 (.out(F));
  Button button_14 (.out(A));
  Button button_15 (.out(A));
  Button button_16 (.out(B));
  Button button_17 (.out(ESPACO));
  Register register_1 (.D(rom_1_data), .en(SEL), .clk(CLK), .Q(register_1_q));  // open: clr
  Button button_18 (.out(U));
  Button button_19 (.out(I));
  Button button_20 (.out(A));
  Button button_21 (.out(A));
  Button button_22 (.out(N));
  Button button_23 (.out(A));
  Bit_Extender #(.out_width(7)) bit_extender_1 (.in(register_1_q), .out(DADOS));
  Button button_24 (.out(CLR));
  Button button_25 (.out(O));
  Button button_26 (.out(A));
  Button button_27 (.out(K));
  Button button_28 (.out(L));
  TTY tty_1 (.data(DADOS), .clk(CLK), .we(SEL), .clr(CLR));

  // Other names for the same wires on the sheet: D = A; E = A; G = A; H = A; J = A; M = A; P = A; S = A; V = A; Y = A

  // Notes on the sheet:
  //   contents of rom_1 (hex, n*v repeats v):
  //   41 42 43 44 45 46 47 48 49 4a 4b 4c 4d 4e 4f 50 51 52 53 54 55 56 57 58 59 5a 20
endmodule
