// Logisim project TecladoASCII.circ as structural Verilog: 2 circuits, main circuit teclado
module teclas (
  input  A,
  input  G,
  input  M,
  input  S,
  input  Y,
  input  B,
  input  H,
  input  N,
  input  T,
  input  Z,
  input  C,
  input  I,
  input  O,
  input  U,
  input  SPC,
  input  D,
  input  J,
  input  P,
  input  V,
  input  E,
  input  K,
  input  Q,
  input  W,
  input  F,
  input  L,
  input  R,
  input  X,
  output [6:0] out_28
);

  assign out_28 = A ? 7'b1000001 : 7'bz;  // Controlled_Buffer controlled_buffer_1
  assign out_28 = B ? 7'b1000010 : 7'bz;  // Controlled_Buffer controlled_buffer_2
  assign out_28 = C ? 7'b1000011 : 7'bz;  // Controlled_Buffer controlled_buffer_3
  assign out_28 = D ? 7'b1000100 : 7'bz;  // Controlled_Buffer controlled_buffer_4
  assign out_28 = E ? 7'b1000101 : 7'bz;  // Controlled_Buffer controlled_buffer_5
  assign out_28 = F ? 7'b1000110 : 7'bz;  // Controlled_Buffer controlled_buffer_6
  assign out_28 = G ? 7'b1000111 : 7'bz;  // Controlled_Buffer controlled_buffer_7
  assign out_28 = H ? 7'b1001000 : 7'bz;  // Controlled_Buffer controlled_buffer_8
  assign out_28 = I ? 7'b1001001 : 7'bz;  // Controlled_Buffer controlled_buffer_9
  assign out_28 = J ? 7'b1001010 : 7'bz;  // Controlled_Buffer controlled_buffer_10
  assign out_28 = K ? 7'b1001011 : 7'bz;  // Controlled_Buffer controlled_buffer_11
  assign out_28 = L ? 7'b1001100 : 7'bz;  // Controlled_Buffer controlled_buffer_12
  assign out_28 = M ? 7'b1001101 : 7'bz;  // Controlled_Buffer controlled_buffer_13
  assign out_28 = N ? 7'b1001110 : 7'bz;  // Controlled_Buffer controlled_buffer_14
  assign out_28 = O ? 7'b1001111 : 7'bz;  // Controlled_Buffer controlled_buffer_15
  assign out_28 = P ? 7'b1010000 : 7'bz;  // Controlled_Buffer controlled_buffer_16
  assign out_28 = Q ? 7'b1010001 : 7'bz;  // Controlled_Buffer controlled_buffer_17
  assign out_28 = R ? 7'b1010010 : 7'bz;  // Controlled_Buffer controlled_buffer_18
  assign out_28 = S ? 7'b1010011 : 7'bz;  // Controlled_Buffer controlled_buffer_19
  assign out_28 = T ? 7'b1010100 : 7'bz;  // Controlled_Buffer controlled_buffer_20
  assign out_28 = U ? 7'b1010101 : 7'bz;  // Controlled_Buffer controlled_buffer_21
  assign out_28 = V ? 7'b1010110 : 7'bz;  // Controlled_Buffer controlled_buffer_22
  assign out_28 = W ? 7'b1010111 : 7'bz;  // Controlled_Buffer controlled_buffer_23
  assign out_28 = X ? 7'b1011000 : 7'bz;  // Controlled_Buffer controlled_buffer_24
  assign out_28 = Y ? 7'b1011001 : 7'bz;  // Controlled_Buffer controlled_buffer_25
  assign out_28 = Z ? 7'b1011010 : 7'bz;  // Controlled_Buffer controlled_buffer_26
  assign out_28 = SPC ? 7'b0100000 : 7'bz;  // Controlled_Buffer controlled_buffer_27

  // Other names for the same wires on the sheet: DADO[6:0] = out_28
endmodule

module teclado (
);

  wire A, B, C, clock_1_out, CLR, D, E, F, G, H, I, J, K, L, M, N, O, P, Q, R, S, SPC, T, U, V, W, X, Y, Z;
  wire [6:0] REF;

  Pull_Resistor pull_resistor_1 (.node(REF));
  teclas teclas_1 (
    .A(A), .G(G), .M(M), .S(S), .Y(Y), .B(B), .H(H), .N(N), .T(T), .Z(Z), .C(C), .I(I), .O(O), .U(U),
    .SPC(SPC), .D(D), .J(J), .P(P), .V(V), .E(E), .K(K), .Q(Q), .W(W), .F(F), .L(L), .R(R), .X(X),
    .out_28(REF));
  Button button_1 (.out(Q));
  Button button_2 (.out(A));
  Button button_3 (.out(W));
  Button button_4 (.out(E));
  Button button_5 (.out(S));
  Button button_6 (.out(D));
  Button button_7 (.out(Z));
  Button button_8 (.out(X));
  Button button_9 (.out(R));
  Button button_10 (.out(T));
  Button button_11 (.out(F));
  Button button_12 (.out(G));
  Button button_13 (.out(C));
  Button button_14 (.out(V));
  Button button_15 (.out(Y));
  Button button_16 (.out(U));
  Button button_17 (.out(H));
  Button button_18 (.out(J));
  Button button_19 (.out(B));
  Button button_20 (.out(N));
  Button button_21 (.out(SPC));
  Button button_22 (.out(I));
  Button button_23 (.out(O));
  Button button_24 (.out(K));
  Button button_25 (.out(L));
  Button button_26 (.out(M));
  Button button_27 (.out(CLR));
  Button button_28 (.out(P));
  Clock clock_1 (.out(clock_1_out));
  TTY tty_1 (.data(REF), .clk(clock_1_out), .we(1'b1), .clr(CLR));
endmodule
